# Fritzing sketch TCC (saved by Fritzing 0.9.3b)
breadboards: 1

parts:
  Componente1 = Arduino Uno (Rev3)
  R2 = Resistor [tolerance=±5% resistance=220 package=THT]
  Mod1 = KY-018 Photoresistor Module [package="Breakout board"]
  Mod2 = KY-015 Temperature & Humidity Sensor Module [package="Breakout board"]
  PCB2 = RTC_DS1302_module
  Componente3 = Arduino MP3 Player Shield
  R1 = Resistor [tolerance=±5% resistance=1k package="2512 [SMD]"]
  Componente4 = Barometric Pressure Sensor - BMP180 Breakout (GY-68)

nets:
  N1: Componente1.A0, R2.Pin_0, Mod2.S, Componente3.A0
  N2: Componente1.A1, Mod1.S, Componente3.A1
  N3: Componente1.A2, Componente1.RESET, Componente3.A2, Componente3.ARST
  N4: Componente1.A3, Componente3.A3
  N5: Componente1.A4/SDA, Componente3.A4, Componente4.SDA
  N6: Componente1.A5/SCL, Componente3.A5, Componente4.SCL
  N7: Componente1.D8, Componente3.5V-MP3-RST
  N8: Componente1.D9_PWM, Componente3.5V-SD-CS
  N9: Componente1.D10_PWM/SS, Componente3.D10
  N10: Componente1.D11_PWM/MOSI, Componente3.5V-MOSI
  N11: Componente1.D12/MISO, Componente3.MISO
  N12: Componente1.D13/SCK, Componente3.5V-SCK
  N13: Componente1.AREF, Componente3.AREF
  N14: Componente1.D0/RX, Componente3.RX
  N15: Componente1.D1/TX, Componente3.TX
  N16: Componente1.D2, PCB2.RST, Componente3.MP3-DREQ
  N17: Componente1.D3_PWM, PCB2.DAT, Componente3.5V-MIDI-RX
  N18: Componente1.D4, PCB2.CLK, Componente3.5V-GPIO1
  N19: Componente1.D5_PWM, Componente3.D5
  N20: Componente1.D6_PWM, Componente3.5V-MP3-CS
  N21: Componente1.D7, Componente3.5V-MP3-DCS
  3V3: Componente1.3V3, Mod1.Vin, Componente3.3.3, R1.Pin_0
  VCC: Componente1.5V, R2.Pin_1, Mod2.Vin, PCB2.VCC, Componente3.VCC
  GND: Componente1.GND, Mod1.-, Mod2.-, PCB2.GND, Componente3.GND, Componente4.GND
  VIN: Componente1.VIN, Componente3.VIN
  N22: R1.Pin_1, Componente4.VCC

custom parts:
  KY-018 Photoresistor Module: KY-018 Photoresistor module, used to measure light intensity. It can determine the presence or absence of light.
  KY-015 Temperature & Humidity Sensor Module: KY-015 temperature and humidity sensor module, provides a low-latency serial interface to measure humidity and temperature.
  RTC_DS1302_module: Arduino module DS1302 SPI Real Time Clock
